// Logisim project adder.circ as structural Verilog
module adder (
  input  Cin,
  input  a,
  input  b,
  output Sum,
  output Cout
);

  wire and_1_out, and_2_out, xor_1_out;

  and and_1 (and_1_out, b, a);
  or or_1 (Cout, and_1_out, and_2_out);
  xor xor_1 (xor_1_out, a, b);
  and and_2 (and_2_out, xor_1_out, Cin);
  xor xor_2 (Sum, Cin, xor_1_out);
endmodule

module _1_Bit_ALU (
  input  Binvert,
  input  CarryIn,
  input  a,
  input  b,
  output Result,
  output CarryOut
);

  wire xor_1_out;

  xor xor_1 (xor_1_out, Binvert, b);
  adder adder_1 (.Cin(CarryIn), .a(a), .b(xor_1_out), .Sum(Result), .Cout(CarryOut));
endmodule

module _16_Bit_ALU (
  input  sub,
  input  [15:0] A,
  input  [15:0] B
);

  wire b0, b1, b2, b3, b4, b5, b6, b7, b8, b9, b10, b11, b12, b13, b14, b15, n1_bit_alu_1_carryout,
       n1_bit_alu_2_carryout, n1_bit_alu_3_carryout, n1_bit_alu_4_carryout, n1_bit_alu_5_carryout,
       n1_bit_alu_6_carryout, n1_bit_alu_7_carryout, n1_bit_alu_8_carryout, n1_bit_alu_9_carryout,
       n1_bit_alu_10_carryout, n1_bit_alu_11_carryout, n1_bit_alu_12_carryout, n1_bit_alu_13_carryout,
       n1_bit_alu_14_carryout, n1_bit_alu_15_carryout;

  _1_Bit_ALU u_1_bit_alu_1 (
    .a(A[0]), .b(b0), .Binvert(sub), .CarryIn(sub), .CarryOut(n1_bit_alu_1_carryout));  // open: Result
  _1_Bit_ALU u_1_bit_alu_2 (
    .a(A[1]), .b(b1), .Binvert(sub), .CarryIn(n1_bit_alu_1_carryout), .CarryOut(n1_bit_alu_2_carryout));  // open: Result
  _1_Bit_ALU u_1_bit_alu_3 (
    .a(A[2]), .b(b2), .Binvert(sub), .CarryIn(n1_bit_alu_2_carryout), .CarryOut(n1_bit_alu_3_carryout));  // open: Result
  _1_Bit_ALU u_1_bit_alu_4 (
    .a(A[3]), .b(b3), .Binvert(sub), .CarryIn(n1_bit_alu_3_carryout), .CarryOut(n1_bit_alu_4_carryout));  // open: Result
  _1_Bit_ALU u_1_bit_alu_5 (
    .a(A[4]), .b(b4), .Binvert(sub), .CarryIn(n1_bit_alu_4_carryout), .CarryOut(n1_bit_alu_5_carryout));  // open: Result
  _1_Bit_ALU u_1_bit_alu_6 (
    .a(A[5]), .b(b5), .Binvert(sub), .CarryIn(n1_bit_alu_5_carryout), .CarryOut(n1_bit_alu_6_carryout));  // open: Result
  _1_Bit_ALU u_1_bit_alu_7 (
    .a(A[6]), .b(b6), .Binvert(sub), .CarryIn(n1_bit_alu_6_carryout), .CarryOut(n1_bit_alu_7_carryout));  // open: Result
  _1_Bit_ALU u_1_bit_alu_8 (
    .a(A[7]), .b(b7), .Binvert(sub), .CarryIn(n1_bit_alu_7_carryout), .CarryOut(n1_bit_alu_8_carryout));  // open: Result
  _1_Bit_ALU u_1_bit_alu_9 (
    .a(A[8]), .b(b8), .Binvert(sub), .CarryIn(n1_bit_alu_8_carryout), .CarryOut(n1_bit_alu_9_carryout));  // open: Result
  _1_Bit_ALU u_1_bit_alu_10 (
    .a(A[9]), .b(b9), .Binvert(sub), .CarryIn(n1_bit_alu_9_carryout), .CarryOut(n1_bit_alu_10_carryout));  // open: Result
  _1_Bit_ALU u_1_bit_alu_11 (
    .a(A[10]), .b(b10), .Binvert(sub), .CarryIn(n1_bit_alu_10_carryout), .CarryOut(n1_bit_alu_11_carryout));  // open: Result
  _1_Bit_ALU u_1_bit_alu_12 (
    .a(A[11]), .b(b11), .Binvert(sub), .CarryIn(n1_bit_alu_11_carryout), .CarryOut(n1_bit_alu_12_carryout));  // open: Result
  _1_Bit_ALU u_1_bit_alu_13 (
    .a(A[12]), .b(b12), .Binvert(sub), .CarryIn(n1_bit_alu_12_carryout), .CarryOut(n1_bit_alu_13_carryout));  // open: Result
  _1_Bit_ALU u_1_bit_alu_14 (
    .a(A[13]), .b(b13), .Binvert(sub), .CarryIn(n1_bit_alu_13_carryout), .CarryOut(n1_bit_alu_14_carryout));  // open: Result
  _1_Bit_ALU u_1_bit_alu_15 (
    .a(A[14]), .b(b14), .Binvert(sub), .CarryIn(n1_bit_alu_14_carryout), .CarryOut(n1_bit_alu_15_carryout));  // open: Result
  _1_Bit_ALU u_1_bit_alu_16 (
    .a(A[15]), .b(b15), .Binvert(sub), .CarryIn(n1_bit_alu_15_carryout));  // open: Result, CarryOut
endmodule
