// Logisim project hw4.circ as structural Verilog: 5 circuits, main circuit Processor
module adder (
  input  Cin,
  input  a,
  input  b,
  output Sum,
  output Cout
);

  wire and_1_out, and_2_out, xor_1_out;

  and and_1 (and_1_out, b, a);
  or or_1 (Cout, and_1_out, and_2_out);
  xor xor_1 (xor_1_out, a, b);
  and and_2 (and_2_out, xor_1_out, Cin);
  xor xor_2 (Sum, Cin, xor_1_out);
endmodule

module _1_Bit_ALU (
  input  Binvert,
  input  CarryIn,
  input  a,
  input  b,
  output Result,
  output CarryOut
);

  wire xor_1_out;

  xor xor_1 (xor_1_out, Binvert, b);
  adder adder_1 (.Cin(CarryIn), .a(a), .b(xor_1_out), .Sum(Result), .Cout(CarryOut));
endmodule

module _16_Bit_ALU (
  input  sub,
  input  [15:0] A,
  input  [15:0] B,
  output [15:0] result,
  output ovf
);

  wire n1_bit_alu_1_carryout, n1_bit_alu_2_carryout, n1_bit_alu_3_carryout, n1_bit_alu_4_carryout,
       n1_bit_alu_5_carryout, n1_bit_alu_6_carryout, n1_bit_alu_7_carryout, n1_bit_alu_8_carryout,
       n1_bit_alu_9_carryout, n1_bit_alu_10_carryout, n1_bit_alu_11_carryout, n1_bit_alu_12_carryout,
       n1_bit_alu_13_carryout, n1_bit_alu_14_carryout, n1_bit_alu_15_carryout, n1_bit_alu_16_carryout;

  _1_Bit_ALU u_1_bit_alu_1 (
    .a(A[0]), .b(B[0]), .Result(result[0]), .Binvert(sub), .CarryIn(sub), .CarryOut(n1_bit_alu_1_carryout));
  _1_Bit_ALU u_1_bit_alu_2 (
    .a(A[1]), .b(B[1]), .Result(result[1]), .Binvert(sub), .CarryIn(n1_bit_alu_1_carryout),
    .CarryOut(n1_bit_alu_2_carryout));
  _1_Bit_ALU u_1_bit_alu_3 (
    .a(A[2]), .b(B[2]), .Result(result[2]), .Binvert(sub), .CarryIn(n1_bit_alu_2_carryout),
    .CarryOut(n1_bit_alu_3_carryout));
  _1_Bit_ALU u_1_bit_alu_4 (
    .a(A[3]), .b(B[3]), .Result(result[3]), .Binvert(sub), .CarryIn(n1_bit_alu_3_carryout),
    .CarryOut(n1_bit_alu_4_carryout));
  _1_Bit_ALU u_1_bit_alu_5 (
    .a(A[4]), .b(B[4]), .Result(result[4]), .Binvert(sub), .CarryIn(n1_bit_alu_4_carryout),
    .CarryOut(n1_bit_alu_5_carryout));
  _1_Bit_ALU u_1_bit_alu_6 (
    .a(A[5]), .b(B[5]), .Result(result[5]), .Binvert(sub), .CarryIn(n1_bit_alu_5_carryout),
    .CarryOut(n1_bit_alu_6_carryout));
  _1_Bit_ALU u_1_bit_alu_7 (
    .a(A[6]), .b(B[6]), .Result(result[6]), .Binvert(sub), .CarryIn(n1_bit_alu_6_carryout),
    .CarryOut(n1_bit_alu_7_carryout));
  _1_Bit_ALU u_1_bit_alu_8 (
    .a(A[7]), .b(B[7]), .Result(result[7]), .Binvert(sub), .CarryIn(n1_bit_alu_7_carryout),
    .CarryOut(n1_bit_alu_8_carryout));
  _1_Bit_ALU u_1_bit_alu_9 (
    .a(A[8]), .b(B[8]), .Result(result[8]), .Binvert(sub), .CarryIn(n1_bit_alu_8_carryout),
    .CarryOut(n1_bit_alu_9_carryout));
  _1_Bit_ALU u_1_bit_alu_10 (
    .a(A[9]), .b(B[9]), .Result(result[9]), .Binvert(sub), .CarryIn(n1_bit_alu_9_carryout),
    .CarryOut(n1_bit_alu_10_carryout));
  _1_Bit_ALU u_1_bit_alu_11 (
    .a(A[10]), .b(B[10]), .Result(result[10]), .Binvert(sub), .CarryIn(n1_bit_alu_10_carryout),
    .CarryOut(n1_bit_alu_11_carryout));
  _1_Bit_ALU u_1_bit_alu_12 (
    .a(A[11]), .b(B[11]), .Result(result[11]), .Binvert(sub), .CarryIn(n1_bit_alu_11_carryout),
    .CarryOut(n1_bit_alu_12_carryout));
  _1_Bit_ALU u_1_bit_alu_13 (
    .a(A[12]), .b(B[12]), .Result(result[12]), .Binvert(sub), .CarryIn(n1_bit_alu_12_carryout),
    .CarryOut(n1_bit_alu_13_carryout));
  _1_Bit_ALU u_1_bit_alu_14 (
    .a(A[13]), .b(B[13]), .Result(result[13]), .Binvert(sub), .CarryIn(n1_bit_alu_13_carryout),
    .CarryOut(n1_bit_alu_14_carryout));
  _1_Bit_ALU u_1_bit_alu_15 (
    .a(A[14]), .b(B[14]), .Result(result[14]), .Binvert(sub), .CarryIn(n1_bit_alu_14_carryout),
    .CarryOut(n1_bit_alu_15_carryout));
  _1_Bit_ALU u_1_bit_alu_16 (
    .a(A[15]), .b(B[15]), .Result(result[15]), .Binvert(sub), .CarryIn(n1_bit_alu_15_carryout),
    .CarryOut(n1_bit_alu_16_carryout));
  xor xor_1 (ovf, n1_bit_alu_15_carryout, n1_bit_alu_16_carryout);
endmodule

module Processor (
  input  reset
);

  wire ALU_ovf, and_1_out;
  wire [15:0] adder_1_out, adder_2_out, multiplexer_1_out, PC_q;

  Register #(.width(16)) PC (.D(multiplexer_1_out), .Q(PC_q), .clr(reset));  // open: en, clk
  Multiplexer #(.width(16)) multiplexer_1 (
    .in0(adder_2_out), .in1(adder_1_out), .out(multiplexer_1_out), .sel(and_1_out));  // open: en
  Adder #(.width(16)) adder_1 (.a(PC_q), .b(16'h4), .out(adder_1_out));  // open: cin, cout
  ROM #(.addrWidth(16), .dataWidth(16)) rom_1 ();  // open: addr, data, sel
  Adder #(.width(16)) adder_2 (.b(adder_1_out), .out(adder_2_out));  // open: a, cin, cout
  RegisterFile RegisterFile ();  // open: Read, Data, rd, rt, rs, reset, rdOut, rtOut, rsOut
  buf and_1 (and_1_out, ALU_ovf);  // AND_Gate
  _16_Bit_ALU ALU (.ovf(ALU_ovf));  // open: sub, A, B, result
  RAM #(.addrWidth(16), .dataWidth(16)) ram_1 (.clr(reset));  // open: addr, data, sel, clk, ld
endmodule

module RegisterFile (
  input  Read,
  input  [15:0] Data,
  input  [2:0] rd,
  input  [2:0] rt,
  input  [2:0] rs,
  input  reset,
  output [15:0] rdOut,
  output [15:0] rtOut,
  output [15:0] rsOut
);

  wire clock_1_out, demultiplexer_1_out0, demultiplexer_1_out1, demultiplexer_1_out2, demultiplexer_1_out3,
       demultiplexer_1_out4, demultiplexer_1_out5, demultiplexer_1_out6, demultiplexer_1_out7;
  wire [15:0] Clock_Trigger_q, r0_q, r1_q, r2_q, r3_q, r4_q, r5_q, r6_q, r7_q;

  Clock clock_1 (.out(clock_1_out));
  Register #(.width(16), .trigger("falling")) Clock_Trigger (
    .D(Data), .Q(Clock_Trigger_q), .clk(clock_1_out));  // open: en, clr
  Demultiplexer #(.select(3)) demultiplexer_1 (
    .out0(demultiplexer_1_out0), .out1(demultiplexer_1_out1), .out2(demultiplexer_1_out2),
    .out3(demultiplexer_1_out3), .out4(demultiplexer_1_out4), .out5(demultiplexer_1_out5),
    .out6(demultiplexer_1_out6), .out7(demultiplexer_1_out7), .in(Read), .sel(rd));  // open: en
  Register #(.width(16), .trigger("high")) r0 (
    .D(Clock_Trigger_q), .Q(r0_q), .clk(demultiplexer_1_out0), .clr(reset));  // open: en
  Register #(.width(16), .trigger("high")) r1 (
    .D(Clock_Trigger_q), .Q(r1_q), .clk(demultiplexer_1_out1), .clr(reset));  // open: en
  Register #(.width(16), .trigger("high")) r2 (
    .D(Clock_Trigger_q), .Q(r2_q), .clk(demultiplexer_1_out2), .clr(reset));  // open: en
  Register #(.width(16), .trigger("high")) r3 (
    .D(Clock_Trigger_q), .Q(r3_q), .clk(demultiplexer_1_out3), .clr(reset));  // open: en
  Register #(.width(16), .trigger("high")) r4 (
    .D(Clock_Trigger_q), .Q(r4_q), .clk(demultiplexer_1_out4), .clr(reset));  // open: en
  Register #(.width(16), .trigger("high")) r5 (
    .D(Clock_Trigger_q), .Q(r5_q), .clk(demultiplexer_1_out5), .clr(reset));  // open: en
  Register #(.width(16), .trigger("high")) r6 (
    .D(Clock_Trigger_q), .Q(r6_q), .clk(demultiplexer_1_out6), .clr(reset));  // open: en
  Register #(.width(16), .trigger("high")) r7 (
    .D(Clock_Trigger_q), .Q(r7_q), .clk(demultiplexer_1_out7), .clr(reset));  // open: en
  Multiplexer #(.select(3), .width(16)) multiplexer_1 (
    .in0(r0_q), .in1(r1_q), .in2(r2_q), .in3(r3_q), .in4(r4_q), .in5(r5_q), .in6(r6_q), .in7(r7_q),
    .out(rdOut), .sel(rd));  // open: en
  Multiplexer #(.select(3), .width(16)) multiplexer_2 (
    .in0(r0_q), .in1(r1_q), .in2(r2_q), .in3(r3_q), .in4(r4_q), .in5(r5_q), .in6(r6_q), .in7(r7_q),
    .out(rtOut), .sel(rt));  // open: en
  Multiplexer #(.select(3), .width(16)) multiplexer_3 (
    .in0(r0_q), .in1(r1_q), .in2(r2_q), .in3(r3_q), .in4(r4_q), .in5(r5_q), .in6(r6_q), .in7(r7_q),
    .out(rsOut), .sel(rs));  // open: en
endmodule
